# Fritzing sketch homeautomation (saved by Fritzing 0.9.3b)

parts:
  Raspberry_Pi_1 = Raspberry Pi 3 [part_number=RPI-3-V1.2]
  LED4 = LEDs [package=led10mm]
  PIR1 = PIR sensor
  CAMERA1 = TTL Serial JPEG Camera  # not connected
  J1 = Basic Servo
  LED5 = LEDs [package=led10mm]

nets:
  3V3: Raspberry_Pi_1.3v3, PIR1.VDD
  N1: Raspberry_Pi_1.GIPO4, LED4.A, PIR1.SIG
  GND: Raspberry_Pi_1.GND, LED4.C, PIR1.GND, J1.gnd, LED5.C
  N2: Raspberry_Pi_1.GIPO17, J1.pulse
  N3: Raspberry_Pi_1.GIPO14, LED5.A
  5V: Raspberry_Pi_1.5V, J1.vcc

notes:
  USB HD camera
  Indication LED
  To door actuator
  PIR sensor to detect preson
  RapberryPi 3 B+

custom parts:
  TTL Serial JPEG Camera: TTL Serial JPEG Camera with NTSC Out
